// Logisim project RISC V.circ as structural Verilog: 14 circuits, main circuit main
module main (
  output [31:0] out_1,
  output [2:0] out_2,
  output [31:0] out_3,
  output [11:0] out_4,
  output [3:0] out_5,
  output [31:0] out_6,
  output [31:0] out_7,
  output [31:0] out_8,
  output [31:0] out_9
);

  wire and_1_out, branch_sel_1_out_4, CL, CLK, control_1_out_4, control_1_out_5, LW, OP_B, or_1_out, SW;
  wire [1:0] IMM_SEL, NEXT_PC, OP_A;
  wire [2:0] FN_3;
  wire [31:0] imm_gen_1_i_imm, imm_gen_1_s_imm, imm_gen_1_u_imm, JALR, multiplexer_2_out, multiplexer_3_out,
       multiplexer_4_out, multiplexer_5_out, ram_1_data, RS_1, RS_2, SB, UJ;

  Clock clock_1 (.out(CLK));
  Button RESET_BUTTON (.out(CL));
  Register #(.width(32)) register_1 (.D(out_1), .Q(out_9), .clk(CLK), .clr(CL));  // open: en
  Multiplexer #(.select(2), .width(32), .enable("false")) multiplexer_1 (
    .in0(out_3), .in1(JALR), .in2(UJ), .in3(multiplexer_2_out), .out(out_1), .sel(NEXT_PC));
  Adder #(.width(32)) adder_1 (.a(out_9), .b(32'h4), .out(out_3));  // open: cin, cout
  Multiplexer #(.width(32), .enable("false")) multiplexer_2 (
    .in0(out_3), .in1(SB), .out(multiplexer_2_out), .sel(and_1_out));
  BRANCH_SEL branch_sel_1 (.in_3(FN_3), .out_4(branch_sel_1_out_4), .RS_1(RS_1), .RS_2(RS_2));
  and and_1 (and_1_out, control_1_out_5, branch_sel_1_out_4);
  ROM #(.addrWidth(12), .dataWidth(32)) rom_1 (
    .addr(out_9[13:2]), .data({out_8[31:15], out_2, out_8[11:0]}));  // open: sel
  CONTROL control_1 (
    .OP_CODE(out_8[6:0]), .out_4(control_1_out_4), .out_5(control_1_out_5), .out_6(SW), .out_7(LW),
    .out_8(OP_A), .out_9(OP_B), .out_10(IMM_SEL), .out_11(NEXT_PC), .out_12(out_5), .in_2(out_2),
    .in_3(out_8[30]));
  REGISTER register_2 (
    .in_1(out_7), .RS_1_READ(RS_1), .RS_1_SEL(out_8[19:15]), .in_4(out_8[11:7]), .in_6(CLK),
    .in_2(control_1_out_4), .RS_2_READ(RS_2), .RS_2_SEL(out_8[24:20]));
  IMM_GEN imm_gen_1 (
    .PC(out_9), .INS({out_8[31:15], out_2, out_8[11:0]}), .i_imm(imm_gen_1_i_imm), .s_imm(imm_gen_1_s_imm),
    .sb_imm(SB), .uj_imm(UJ), .u_imm(imm_gen_1_u_imm));
  Multiplexer #(.select(2), .width(32)) multiplexer_3 (
    .in0(imm_gen_1_i_imm), .in1(imm_gen_1_s_imm), .in2(imm_gen_1_u_imm), .out(multiplexer_3_out),
    .sel(IMM_SEL));  // open: in3, en
  Multiplexer #(.select(2), .width(32), .enable("false")) multiplexer_4 (
    .in0(RS_1), .in1(out_9), .in2(out_3), .in3({32{1'b0}}), .out(multiplexer_4_out), .sel(OP_A));
  Multiplexer #(.width(32), .enable("false")) multiplexer_5 (
    .in0(RS_2), .in1(multiplexer_3_out), .out(multiplexer_5_out), .sel(OP_B));
  Adder #(.width(32)) adder_2 (.a(RS_1), .b(imm_gen_1_i_imm), .out(JALR));  // open: cin, cout
  ALU alu_1 (
    .Operand_A(multiplexer_4_out), .Operand_B(multiplexer_5_out),
    .ALU_out({out_6[31:14], out_4, out_6[1:0]}), .Alu_Out_Select(out_5));
  or or_1 (or_1_out, SW, LW);
  RAM #(.addrWidth(12), .dataWidth(32), .bus("separate")) ram_1 (
    .addr(out_4), .din(RS_2), .data(ram_1_data), .str(SW), .sel(or_1_out), .clk(CLK), .ld(LW), .clr(CL));
  Multiplexer #(.width(32), .enable("false")) multiplexer_6 (
    .in0({out_6[31:14], out_4, out_6[1:0]}), .in1(ram_1_data), .out(out_7), .sel(LW));

  assign out_6[13:2] = out_4;
  assign out_8[14:12] = out_2;

  // Other names for the same wires on the sheet: ALU[3:0] = out_5; FN3[2:0] = out_2; WD[31:0] = out_7

  // Notes on the sheet:
  //   contents of rom_1 (hex, n*v repeats v):
  //   c00293 329313 62a823
endmodule

module NEXT_PC (
  input  SB,
  input  JAL,
  input  JALR,
  output A,
  output B
);

  or or_1 (A, JALR, SB);
  or or_2 (B, JAL, SB);
endmodule

module CONTROL_DECODE (
  input  R_Type,
  input  I_Type,
  input  Load,
  input  JALR,
  input  Store,
  input  Branch,
  input  Auipc,
  input  Lui,
  input  JAL,
  input  [2:0] FN_3,
  input  FN_7,
  output REG_Write,
  output Branch_2,
  output Store_2,
  output Mem_2_Reg,
  output [1:0] OPERAND_A,
  output OPERAND_B,
  output [1:0] IMM_SELECTOR,
  output [1:0] NEXT_PC,
  output OUT_0,
  output OUT_1,
  output OUT_2,
  output OUT_3
);

  wire alu_c_1_alu_0, alu_c_1_alu_1, alu_c_1_alu_2, or_1_out, or_2_out, or_3_out;

  or or_1 (or_1_out, R_Type, I_Type, Load, JALR, Store);
  or or_2 (or_2_out, Lui, Auipc);
  or or_3 (or_3_out, JALR, JAL);
  or or_4 (OPERAND_B, I_Type, Lui, JALR, Auipc, Store);
  or or_5 (REG_Write, R_Type, I_Type, Load, JALR, Auipc, Lui, JAL);
  OPERAND_A operand_a_1 (
    .JAL_JALR(or_3_out), .AUIPC(Auipc), .RS_1(or_1_out), .ZERO(1'b0), ._0(OPERAND_A[1]), .out1(OPERAND_A[0]));
  IMM_SELECTOR imm_selector_1 (
    .STYPE(Store), .UTYPE(or_2_out), .IType(I_Type), ._0(IMM_SELECTOR[1]), ._1(IMM_SELECTOR[0]));
  NEXT_PC next_pc_1 (.SB(Branch), .JAL(JAL), .JALR(JALR), .A(NEXT_PC[1]), .B(NEXT_PC[0]));
  ALU_C alu_c_1 (
    .R_TYPE(R_Type), .I_TYPE(I_Type), .LOAD(Load), .JALR(JALR), .STORE(Store), .AUIPC(Auipc), .LUI(Lui),
    .JAL(JAL), .ALU_0(alu_c_1_alu_0), .ALU_1(alu_c_1_alu_1), .ALU_2(alu_c_1_alu_2));
  ALU_CONTROL alu_control_1 (
    .ALU_OP_2(alu_c_1_alu_0), .ALU_OP_1(alu_c_1_alu_1), .ALU_OP_0(alu_c_1_alu_2), .FN_3_2(FN_3[2]),
    .FN_3_1(FN_3[1]), .FN_3_0(FN_3[0]), .FN_7(FN_7), .ALU_OUT_0(OUT_0), .ALU_OUT_1(OUT_1), .ALU_OUT_2(OUT_2),
    .ALU_OUT_3(OUT_3));

  assign Branch_2 = Branch;
  assign Mem_2_Reg = Load;
  assign Store_2 = Store;
endmodule

module OPERAND_A (
  input  JAL_JALR,
  input  AUIPC,
  input  RS_1,
  input  ZERO,
  output _0,
  output out1
);

  wire and_1_out, and_2_out, and_3_out, and_4_out, and_5_out, not_1_out, not_2_out, not_3_out, not_4_out,
       not_5_out, not_6_out, not_7_out, not_8_out, not_9_out, not_10_out, not_11_out, not_12_out, not_13_out,
       not_14_out;

  not not_1 (not_1_out, JAL_JALR);
  not not_2 (not_2_out, AUIPC);
  and and_1 (and_1_out, not_1_out, not_2_out, not_3_out);
  not not_3 (not_3_out, RS_1);
  not not_4 (not_4_out, JAL_JALR);
  and and_2 (and_2_out, not_4_out, not_5_out, ZERO);
  not not_5 (not_5_out, RS_1);
  not not_6 (not_6_out, JAL_JALR);
  and and_3 (and_3_out, not_6_out, not_7_out, not_8_out);
  not not_7 (not_7_out, AUIPC);
  not not_8 (not_8_out, RS_1);
  not not_9 (not_9_out, JAL_JALR);
  not not_10 (not_10_out, RS_1);
  and and_4 (and_4_out, not_9_out, not_10_out, not_11_out);
  not not_11 (not_11_out, ZERO);
  not not_12 (not_12_out, AUIPC);
  not not_13 (not_13_out, RS_1);
  and and_5 (and_5_out, not_12_out, not_13_out, not_14_out);
  not not_14 (not_14_out, ZERO);
  or or_1 (_0, and_1_out, and_2_out);
  or or_2 (out1, and_3_out, and_4_out, and_5_out);
endmodule

module IMM_SELECTOR (
  input  STYPE,
  input  UTYPE,
  input  IType,
  output _0,
  output _1
);

  wire not_1_out, not_2_out, not_3_out, not_4_out;

  not not_1 (not_1_out, STYPE);
  not not_2 (not_2_out, IType);
  not not_3 (not_3_out, UTYPE);
  not not_4 (not_4_out, IType);
  and and_1 (_0, not_1_out, not_2_out);
  and and_2 (_1, not_3_out, not_4_out);
endmodule

module ALU_C (
  input  R_TYPE,
  input  I_TYPE,
  input  LOAD,
  input  JALR,
  input  STORE,
  input  AUIPC,
  input  LUI,
  input  JAL,
  output ALU_0,
  output ALU_1,
  output ALU_2
);

  wire or_1_out, or_2_out, or_3_out, or_4_out, or_5_out, or_6_out;

  or or_1 (or_1_out, JAL, LUI);
  or or_2 (or_2_out, AUIPC, STORE);
  or or_3 (or_3_out, JAL, LUI);
  or or_4 (or_4_out, JALR, LOAD);
  or or_5 (or_5_out, JAL, AUIPC);
  or or_6 (or_6_out, JALR, I_TYPE);
  or or_7 (ALU_0, or_1_out, or_2_out);
  or or_8 (ALU_1, or_3_out, or_4_out);
  or or_9 (ALU_2, or_5_out, or_6_out);
endmodule

module ALU_CONTROL (
  input  ALU_OP_2,
  input  ALU_OP_1,
  input  ALU_OP_0,
  input  FN_3_2,
  input  FN_3_1,
  input  FN_3_0,
  input  FN_7,
  output ALU_OUT_0,
  output ALU_OUT_1,
  output ALU_OUT_2,
  output ALU_OUT_3
);

  wire and_1_out, and_2_out, and_3_out, and_4_out, and_5_out, and_6_out, and_7_out, and_8_out, and_9_out,
       and_10_out, and_11_out, and_12_out, and_13_out, and_14_out, and_15_out, and_16_out, and_17_out,
       and_18_out, and_19_out, and_20_out, not_1_out, not_2_out, not_3_out, not_4_out, not_5_out, not_6_out,
       not_7_out, not_8_out, not_9_out, not_10_out, not_11_out, not_12_out, not_13_out, not_14_out,
       not_15_out, not_16_out, not_17_out, not_18_out, not_19_out, not_20_out, not_21_out, not_22_out,
       not_23_out, not_24_out, not_25_out, not_26_out, not_27_out, not_28_out, not_29_out, not_30_out,
       not_31_out, not_32_out, not_33_out, not_34_out, not_35_out, not_36_out, not_37_out, not_38_out;

  not not_1 (not_1_out, ALU_OP_2);
  not not_2 (not_2_out, FN_3_1);
  not not_3 (not_3_out, ALU_OP_2);
  not not_4 (not_4_out, ALU_OP_2);
  not not_5 (not_5_out, ALU_OP_1);
  not not_6 (not_6_out, FN_3_2);
  not not_7 (not_7_out, ALU_OP_2);
  not not_8 (not_8_out, ALU_OP_0);
  not not_9 (not_9_out, ALU_OP_2);
  not not_10 (not_10_out, ALU_OP_1);
  not not_11 (not_11_out, FN_3_1);
  not not_12 (not_12_out, FN_3_0);
  not not_13 (not_13_out, FN_7);
  not not_14 (not_14_out, ALU_OP_2);
  not not_15 (not_15_out, FN_3_1);
  not not_16 (not_16_out, FN_3_0);
  not not_17 (not_17_out, ALU_OP_2);
  not not_18 (not_18_out, FN_3_2);
  not not_19 (not_19_out, ALU_OP_2);
  not not_20 (not_20_out, ALU_OP_0);
  not not_21 (not_21_out, FN_3_0);
  not not_22 (not_22_out, ALU_OP_2);
  not not_23 (not_23_out, FN_3_0);
  not not_24 (not_24_out, ALU_OP_2);
  not not_25 (not_25_out, ALU_OP_2);
  not not_26 (not_26_out, ALU_OP_2);
  not not_27 (not_27_out, ALU_OP_0);
  not not_28 (not_28_out, FN_3_1);
  not not_29 (not_29_out, ALU_OP_2);
  not not_30 (not_30_out, FN_3_2);
  not not_31 (not_31_out, FN_3_1);
  not not_32 (not_32_out, ALU_OP_2);
  not not_33 (not_33_out, FN_3_1);
  not not_34 (not_34_out, ALU_OP_2);
  not not_35 (not_35_out, ALU_OP_1);
  not not_36 (not_36_out, FN_3_0);
  and and_1 (and_1_out, not_1_out, FN_3_2, not_2_out, FN_3_0);
  and and_2 (and_2_out, not_3_out, ALU_OP_1);
  and and_3 (and_3_out, ALU_OP_1, ALU_OP_0);
  not not_37 (not_37_out, ALU_OP_2);
  not not_38 (not_38_out, FN_3_2);
  and and_4 (and_4_out, not_37_out, not_38_out, FN_3_0);
  and and_5 (and_5_out, not_4_out, not_5_out, not_6_out, FN_3_1);
  and and_6 (and_6_out, not_7_out, not_8_out, FN_3_1, FN_3_0);
  and and_7 (and_7_out, not_9_out, not_10_out, FN_3_2, not_11_out, not_12_out, not_13_out);
  and and_8 (and_8_out, not_14_out, ALU_OP_0, FN_3_2, not_15_out, not_16_out);
  and and_9 (and_9_out, ALU_OP_1, ALU_OP_0);
  and and_10 (and_10_out, not_17_out, not_18_out, FN_3_0);
  and and_11 (and_11_out, not_19_out, not_20_out, FN_3_2, not_21_out, FN_7);
  and and_12 (and_12_out, not_22_out, FN_3_2, FN_3_1, not_23_out);
  and and_13 (and_13_out, not_24_out, ALU_OP_0, FN_3_1, FN_3_0);
  and and_14 (and_14_out, not_25_out, ALU_OP_1);
  and and_15 (and_15_out, ALU_OP_1, ALU_OP_0);
  and and_16 (and_16_out, not_26_out, not_27_out, not_28_out, FN_7);
  and and_17 (and_17_out, not_29_out, not_30_out, not_31_out, FN_3_0);
  and and_18 (and_18_out, not_32_out, not_33_out, FN_3_0, FN_7);
  and and_19 (and_19_out, not_34_out, not_35_out, FN_3_1, not_36_out);
  and and_20 (and_20_out, ALU_OP_1, ALU_OP_0);
  or or_1 (ALU_OUT_0, and_1_out, and_2_out, and_3_out);
  or or_2 (ALU_OUT_2, and_10_out, and_11_out, and_12_out, and_13_out, and_14_out, and_15_out);
  or or_3 (ALU_OUT_3, and_16_out, and_17_out, and_18_out, and_19_out, and_20_out);
  or or_4 (ALU_OUT_1, and_4_out, and_5_out, and_6_out, and_7_out, and_8_out, and_9_out);
endmodule

module IMM_GEN (
  input  [31:0] INS,
  input  [31:0] PC,
  output [31:0] i_imm,
  output [31:0] s_imm,
  output [31:0] sb_imm,
  output [31:0] uj_imm,
  output [31:0] u_imm
);

  wire [31:0] bit_extender_3_out, bit_extender_4_out, bit_extender_5_out;

  assign i_imm = {{20{INS[31]}}, INS[31:20]};  // Bit_Extender bit_extender_1
  assign s_imm = {{20{INS[31]}}, {INS[31:25], INS[11:7]}};  // Bit_Extender bit_extender_2
  assign bit_extender_3_out = {{19{INS[31]}}, {INS[31], INS[7], INS[30:25], INS[11:8], 1'b0}};  // Bit_Extender bit_extender_3
  assign bit_extender_4_out = {{11{INS[31]}}, {INS[31], INS[19:12], INS[20], INS[30:21], 1'b0}};  // Bit_Extender bit_extender_4
  assign bit_extender_5_out = {{12{1'b0}}, INS[31:12]};  // Bit_Extender bit_extender_5
  Adder #(.width(32)) adder_1 (.a(bit_extender_3_out), .b(PC), .out(sb_imm));  // open: cin, cout
  Adder #(.width(32)) adder_2 (.a(bit_extender_4_out), .b(PC), .out(uj_imm));  // open: cin, cout
  Shifter #(.width(32)) shifter_1 (.in(bit_extender_5_out), .\dist (5'b01100), .out(u_imm));
endmodule

module TYPE_DECODE (
  input  [6:0] in_1,
  output R_TYPE,
  output I_TYPE,
  output LOAD,
  output JALR,
  output STORE,
  output BRANCH,
  output AUIPC,
  output LUI,
  output JAL
);

  Comparator #(.width(7)) comparator_1 (.a(in_1), .b(7'b0110011), .eq(R_TYPE));  // open: gt, lt
  Comparator #(.width(7)) comparator_2 (.a(in_1), .b(7'b0010011), .eq(I_TYPE));  // open: gt, lt
  Comparator #(.width(7)) comparator_3 (.a(in_1), .b(7'b0000011), .eq(LOAD));  // open: gt, lt
  Comparator #(.width(7)) comparator_4 (.a(in_1), .b(7'b1100111), .eq(JALR));  // open: gt, lt
  Comparator #(.width(7)) comparator_5 (.a(in_1), .b(7'b0100011), .eq(STORE));  // open: gt, lt
  Comparator #(.width(7)) comparator_6 (.a(in_1), .b(7'b1100011), .eq(BRANCH));  // open: gt, lt
  Comparator #(.width(7)) comparator_7 (.a(in_1), .b(7'b0010111), .eq(AUIPC));  // open: gt, lt
  Comparator #(.width(7)) comparator_8 (.a(in_1), .b(7'b0110111), .eq(LUI));  // open: gt, lt
  Comparator #(.width(7)) comparator_9 (.a(in_1), .b(7'b1101111), .eq(JAL));  // open: gt, lt
endmodule

module REGISTER (
  input  [31:0] in_1,
  input  in_2,
  input  [4:0] RS_1_SEL,
  input  [4:0] in_4,
  input  [4:0] RS_2_SEL,
  input  in_6,
  output [31:0] RS_1_READ,
  output [31:0] RS_2_READ
);

  wire decoder_1_out1, decoder_1_out2, decoder_1_out3, decoder_1_out4, decoder_1_out5, decoder_1_out6,
       decoder_1_out7, decoder_1_out8, decoder_1_out9, decoder_1_out10, decoder_1_out11, decoder_1_out12,
       decoder_1_out13, decoder_1_out14, decoder_1_out15, decoder_1_out16, decoder_1_out17, decoder_1_out18,
       decoder_1_out19, decoder_1_out20, decoder_1_out21, decoder_1_out22, decoder_1_out23, decoder_1_out24,
       decoder_1_out25, decoder_1_out26, decoder_1_out27, decoder_1_out28, decoder_1_out29, decoder_1_out30,
       decoder_1_out31;
  wire [31:0] register_1_q, register_2_q, register_3_q, register_4_q, register_5_q, register_6_q,
       register_7_q, register_8_q, register_9_q, register_10_q, register_11_q, register_12_q, register_13_q,
       register_14_q, register_15_q, register_16_q, register_17_q, register_18_q, register_19_q,
       register_20_q, register_21_q, register_22_q, register_23_q, register_24_q, register_25_q,
       register_26_q, register_27_q, register_28_q, register_29_q, register_30_q, register_31_q;

  Decoder #(.select(5), .disabled(0)) decoder_1 (
    .out1(decoder_1_out1), .out2(decoder_1_out2), .out3(decoder_1_out3), .out4(decoder_1_out4),
    .out5(decoder_1_out5), .out6(decoder_1_out6), .out7(decoder_1_out7), .out8(decoder_1_out8),
    .out9(decoder_1_out9), .out10(decoder_1_out10), .out11(decoder_1_out11), .out12(decoder_1_out12),
    .out13(decoder_1_out13), .out14(decoder_1_out14), .out15(decoder_1_out15), .out16(decoder_1_out16),
    .out17(decoder_1_out17), .out18(decoder_1_out18), .out19(decoder_1_out19), .out20(decoder_1_out20),
    .out21(decoder_1_out21), .out22(decoder_1_out22), .out23(decoder_1_out23), .out24(decoder_1_out24),
    .out25(decoder_1_out25), .out26(decoder_1_out26), .out27(decoder_1_out27), .out28(decoder_1_out28),
    .out29(decoder_1_out29), .out30(decoder_1_out30), .out31(decoder_1_out31), .sel(in_4), .en(in_2));  // open: out0
  Register #(.width(32)) register_1 (.D(in_1), .en(decoder_1_out1), .Q(register_1_q), .clk(in_6));  // open: clr
  Register #(.width(32)) register_2 (.D(in_1), .en(decoder_1_out2), .Q(register_2_q), .clk(in_6));  // open: clr
  Register #(.width(32)) register_3 (.D(in_1), .en(decoder_1_out3), .Q(register_3_q), .clk(in_6));  // open: clr
  Register #(.width(32)) register_4 (.D(in_1), .en(decoder_1_out4), .Q(register_4_q), .clk(in_6));  // open: clr
  Register #(.width(32)) register_5 (.D(in_1), .en(decoder_1_out5), .Q(register_5_q), .clk(in_6));  // open: clr
  Register #(.width(32)) register_6 (.D(in_1), .en(decoder_1_out6), .Q(register_6_q), .clk(in_6));  // open: clr
  Register #(.width(32)) register_7 (.D(in_1), .en(decoder_1_out7), .Q(register_7_q), .clk(in_6));  // open: clr
  Register #(.width(32)) register_8 (.D(in_1), .en(decoder_1_out8), .Q(register_8_q), .clk(in_6));  // open: clr
  Register #(.width(32)) register_9 (.D(in_1), .en(decoder_1_out9), .Q(register_9_q), .clk(in_6));  // open: clr
  Register #(.width(32)) register_10 (.D(in_1), .en(decoder_1_out10), .Q(register_10_q), .clk(in_6));  // open: clr
  Register #(.width(32)) register_11 (.D(in_1), .en(decoder_1_out11), .Q(register_11_q), .clk(in_6));  // open: clr
  Register #(.width(32)) register_12 (.D(in_1), .en(decoder_1_out12), .Q(register_12_q), .clk(in_6));  // open: clr
  Register #(.width(32)) register_13 (.D(in_1), .en(decoder_1_out13), .Q(register_13_q), .clk(in_6));  // open: clr
  Register #(.width(32)) register_14 (.D(in_1), .en(decoder_1_out14), .Q(register_14_q), .clk(in_6));  // open: clr
  Register #(.width(32)) register_15 (.D(in_1), .en(decoder_1_out15), .Q(register_15_q), .clk(in_6));  // open: clr
  Register #(.width(32)) register_16 (.D(in_1), .en(decoder_1_out16), .Q(register_16_q), .clk(in_6));  // open: clr
  Register #(.width(32)) register_17 (.D(in_1), .en(decoder_1_out17), .Q(register_17_q), .clk(in_6));  // open: clr
  Register #(.width(32)) register_18 (.D(in_1), .en(decoder_1_out18), .Q(register_18_q), .clk(in_6));  // open: clr
  Register #(.width(32)) register_19 (.D(in_1), .en(decoder_1_out19), .Q(register_19_q), .clk(in_6));  // open: clr
  Register #(.width(32)) register_20 (.D(in_1), .en(decoder_1_out20), .Q(register_20_q), .clk(in_6));  // open: clr
  Register #(.width(32)) register_21 (.D(in_1), .en(decoder_1_out21), .Q(register_21_q), .clk(in_6));  // open: clr
  Register #(.width(32)) register_22 (.D(in_1), .en(decoder_1_out22), .Q(register_22_q), .clk(in_6));  // open: clr
  Register #(.width(32)) register_23 (.D(in_1), .en(decoder_1_out23), .Q(register_23_q), .clk(in_6));  // open: clr
  Register #(.width(32)) register_24 (.D(in_1), .en(decoder_1_out24), .Q(register_24_q), .clk(in_6));  // open: clr
  Register #(.width(32)) register_25 (.D(in_1), .en(decoder_1_out25), .Q(register_25_q), .clk(in_6));  // open: clr
  Register #(.width(32)) register_26 (.D(in_1), .en(decoder_1_out26), .Q(register_26_q), .clk(in_6));  // open: clr
  Register #(.width(32)) register_27 (.D(in_1), .en(decoder_1_out27), .Q(register_27_q), .clk(in_6));  // open: clr
  Register #(.width(32)) register_28 (.D(in_1), .en(decoder_1_out28), .Q(register_28_q), .clk(in_6));  // open: clr
  Register #(.width(32)) register_29 (.D(in_1), .en(decoder_1_out29), .Q(register_29_q), .clk(in_6));  // open: clr
  Register #(.width(32)) register_30 (.D(in_1), .en(decoder_1_out30), .Q(register_30_q), .clk(in_6));  // open: clr
  Register #(.width(32)) register_31 (.D(in_1), .en(decoder_1_out31), .Q(register_31_q), .clk(in_6));  // open: clr
  Multiplexer #(.select(5), .width(32), .enable("false")) multiplexer_1 (
    .in0({32{1'b0}}), .in1(register_1_q), .in2(register_2_q), .in3(register_3_q), .in4(register_4_q),
    .in5(register_5_q), .in6(register_6_q), .in7(register_7_q), .in8(register_8_q), .in9(register_9_q),
    .in10(register_10_q), .in11(register_11_q), .in12(register_12_q), .in13(register_13_q),
    .in14(register_14_q), .in15(register_15_q), .in16(register_16_q), .in17(register_17_q),
    .in18(register_18_q), .in19(register_19_q), .in20(register_20_q), .in21(register_21_q),
    .in22(register_22_q), .in23(register_23_q), .in24(register_24_q), .in25(register_25_q),
    .in26(register_26_q), .in27(register_27_q), .in28(register_28_q), .in29(register_29_q),
    .in30(register_30_q), .in31(register_31_q), .out(RS_1_READ), .sel(RS_1_SEL));
  Multiplexer #(.select(5), .width(32), .enable("false")) multiplexer_2 (
    .in0({32{1'b0}}), .in1(register_1_q), .in2(register_2_q), .in3(register_3_q), .in4(register_4_q),
    .in5(register_5_q), .in6(register_6_q), .in7(register_7_q), .in8(register_8_q), .in9(register_9_q),
    .in10(register_10_q), .in11(register_11_q), .in12(register_12_q), .in13(register_13_q),
    .in14(register_14_q), .in15(register_15_q), .in16(register_16_q), .in17(register_17_q),
    .in18(register_18_q), .in19(register_19_q), .in20(register_20_q), .in21(register_21_q),
    .in22(register_22_q), .in23(register_23_q), .in24(register_24_q), .in25(register_25_q),
    .in26(register_26_q), .in27(register_27_q), .in28(register_28_q), .in29(register_29_q),
    .in30(register_30_q), .in31(register_31_q), .out(RS_2_READ), .sel(RS_2_SEL));
endmodule

module CONTROL (
  input  [6:0] OP_CODE,
  input  [2:0] in_2,
  input  in_3,
  output out_4,
  output out_5,
  output out_6,
  output out_7,
  output [1:0] out_8,
  output out_9,
  output [1:0] out_10,
  output [1:0] out_11,
  output [3:0] out_12
);

  wire type_decode_1_auipc, type_decode_1_branch, type_decode_1_i_type, type_decode_1_jal,
       type_decode_1_jalr, type_decode_1_load, type_decode_1_lui, type_decode_1_r_type, type_decode_1_store;

  TYPE_DECODE type_decode_1 (
    .in_1(OP_CODE), .R_TYPE(type_decode_1_r_type), .I_TYPE(type_decode_1_i_type), .LOAD(type_decode_1_load),
    .JALR(type_decode_1_jalr), .STORE(type_decode_1_store), .BRANCH(type_decode_1_branch),
    .AUIPC(type_decode_1_auipc), .LUI(type_decode_1_lui), .JAL(type_decode_1_jal));
  CONTROL_DECODE control_decode_1 (
    .FN_3(in_2), .FN_7(in_3), .REG_Write(out_4), .Branch_2(out_5), .Store_2(out_6), .Mem_2_Reg(out_7),
    .OPERAND_A(out_8), .OPERAND_B(out_9), .IMM_SELECTOR(out_10), .NEXT_PC(out_11),
    .R_Type(type_decode_1_r_type), .I_Type(type_decode_1_i_type), .Load(type_decode_1_load),
    .JALR(type_decode_1_jalr), .Store(type_decode_1_store), .Branch(type_decode_1_branch),
    .Auipc(type_decode_1_auipc), .Lui(type_decode_1_lui), .JAL(type_decode_1_jal), .OUT_0(out_12[3]),
    .OUT_1(out_12[2]), .OUT_2(out_12[1]), .OUT_3(out_12[0]));
endmodule

module ALU (
  input  [31:0] Operand_A,
  input  [31:0] Operand_B,
  input  [3:0] Alu_Out_Select,
  output [31:0] ALU_out
);

  wire comparator_1_lt, comparator_2_lt;
  wire [31:0] adder_1_out, and_1_out, bit_extender_1_out, bit_extender_2_out, or_1_out, shifter_1_out,
       shifter_2_out, shifter_3_out, subtractor_1_out, xor_1_out;

  Adder #(.width(32)) adder_1 (.a(Operand_A), .b(Operand_B), .out(adder_1_out));  // open: cin, cout
  Subtractor #(.width(32)) subtractor_1 (.a(Operand_A), .b(Operand_B), .out(subtractor_1_out));  // open: bin, bout
  Comparator #(.width(32)) comparator_1 (.a(Operand_A), .b(Operand_B), .lt(comparator_1_lt));  // open: gt, eq
  Comparator #(.width(32), .mode("unsigned")) comparator_2 (
    .a(Operand_A), .b(Operand_B), .lt(comparator_2_lt));  // open: gt, eq
  Shifter #(.width(32)) shifter_1 (.in(Operand_A), .\dist (Operand_B[4:0]), .out(shifter_1_out));
  assign xor_1_out = Operand_A ^ Operand_B;  // XOR_Gate xor_1, 32 bits wide
  assign and_1_out = Operand_A & Operand_B;  // AND_Gate and_1, 32 bits wide
  assign or_1_out = Operand_A | Operand_B;  // OR_Gate or_1, 32 bits wide
  Shifter #(.width(32), .shift("ar")) shifter_2 (.in(Operand_A), .\dist (Operand_B[4:0]), .out(shifter_2_out));
  Shifter #(.width(32), .shift("lr")) shifter_3 (.in(Operand_A), .\dist (Operand_B[4:0]), .out(shifter_3_out));
  assign bit_extender_1_out = {{31{1'b0}}, comparator_1_lt};  // Bit_Extender bit_extender_1
  assign bit_extender_2_out = {{31{1'b0}}, comparator_2_lt};  // Bit_Extender bit_extender_2
  Multiplexer #(.select(4), .width(32)) multiplexer_1 (
    .in0(adder_1_out), .in1(subtractor_1_out), .in2(and_1_out), .in3(or_1_out), .in4(xor_1_out),
    .in5(bit_extender_1_out), .in6(bit_extender_2_out), .in7(shifter_1_out), .in8(shifter_3_out),
    .in9(shifter_2_out), .in15(Operand_A), .out(ALU_out), .sel(Alu_Out_Select));  // open: in10, in11, in12, in13, in14, en
endmodule

module BRANCH_SEL (
  input  [31:0] RS_2,
  input  [31:0] RS_1,
  input  [2:0] in_3,
  output out_4
);

  wire comparator_1_eq, comparator_2_eq, comparator_3_lt, comparator_4_eq, comparator_4_gt, comparator_5_lt,
       comparator_6_eq, comparator_6_gt, not_1_out, or_1_out, or_2_out;

  Comparator #(.width(32)) comparator_1 (.a(RS_1), .b(RS_2), .eq(comparator_1_eq));  // open: gt, lt
  Comparator #(.width(32)) comparator_2 (.a(RS_1), .b(RS_2), .eq(comparator_2_eq));  // open: gt, lt
  Comparator #(.width(32)) comparator_3 (.a(RS_1), .b(RS_2), .lt(comparator_3_lt));  // open: gt, eq
  Comparator #(.width(32)) comparator_4 (.a(RS_1), .b(RS_2), .gt(comparator_4_gt), .eq(comparator_4_eq));  // open: lt
  Comparator #(.width(32), .mode("unsigned")) comparator_5 (.a(RS_1), .b(RS_2), .lt(comparator_5_lt));  // open: gt, eq
  Comparator #(.width(32), .mode("unsigned")) comparator_6 (
    .a(RS_1), .b(RS_2), .gt(comparator_6_gt), .eq(comparator_6_eq));  // open: lt
  or or_1 (or_1_out, comparator_4_gt, comparator_4_eq);
  or or_2 (or_2_out, comparator_6_gt, comparator_6_eq);
  not not_1 (not_1_out, comparator_2_eq);
  Multiplexer #(.select(3), .enable("false")) multiplexer_1 (
    .in0(comparator_1_eq), .in1(not_1_out), .in4(comparator_3_lt), .in5(or_1_out), .in6(comparator_5_lt),
    .in7(or_2_out), .out(out_4), .sel(in_3));  // open: in2, in3

  // Notes on the sheet:
  //   beq
  //   bne
  //   blt
  //   bge
  //   bltu
  //   bgeu
endmodule

module ALU_OP (
  input  R,
  input  I,
  input  LOAD,
  input  STORE,
  input  JAL,
  input  JALR,
  input  AUIPC,
  input  LUI,
  output O1,
  output O2,
  output O3
);

  or or_1 (O1, LUI, AUIPC, JALR, JAL);
  or or_2 (O2, LUI, AUIPC, STORE, LOAD);
  or or_3 (O3, LUI, JALR, STORE, I);

  // Notes on the sheet:
  //   ALU OP
endmodule
